# Fritzing sketch SiKoGen (saved by Fritzing 0.9.2b)
breadboards: 1

parts:
  IC1 = 3W33DC15DC [package=DIL]
  IC2 = 3W33DC15DC [package=DIL]
  VCC1 = Battery
  D1 = Zener Diode [part_number=1N4732A breakdown_voltage=5.1V package="300 mil [THT]"]
  D3 = Schottky Diode [part_number=1N5817 package="300 mil [THT]"]  # not connected
  R1 = Resistor [tolerance=±5% resistance=2.2k package=THT]
  U1 = Voltage Regulator [package=to220-adj]
  R2 = Resistor [tolerance=±5% resistance=220 package=THT]
  R3 = Resistor [tolerance=±5% resistance=33 package=THT]
  LED1 = LED - 3mm [color="Blue (470nm)" package="3 mm [THT]"]

nets:
  VIN: IC1.VIN, IC2.VIN, VCC1.+, D1.cathode
  N1: IC1.GND#4, IC2.GND#4, VCC1.-, D1.anode
  N2: IC1.+Vo, IC2.-Vo
  N3: IC2.+Vo, R1.Pin_0
  N4: R1.Pin_1, U1.IN
  N5: U1.ADJ, R2.Pin_0, LED1.cathode
  N6: U1.OUT, R3.Pin_1
  N7: R2.Pin_1, R3.Pin_0
